// Logisim project Project1.circ as structural Verilog: 1 circuit, main circuit main
module main (
  input  A,
  input  B,
  input  C,
  output out_4
);

  wire A_B_prime_out, B_C_out, not_1_out;

  not not_1 (not_1_out, B);
  and A_B_prime (A_B_prime_out, A, A, not_1_out);
  and B_C (B_C_out, B, C);
  or or_1 (out_4, A_B_prime_out, B_C_out);

  // Notes on the sheet:
  //   (A*B') + (B*C)
endmodule
